# Fritzing sketch knack_lampa (saved by Fritzing 0.9.3b)
circuit board: 8.46667cm x 5.64444cm
breadboards: 1

parts:
  LED1 = LED - 5mm [color="Red (633nm)" package="5 mm [THT]"]
  R1 = Resistor [tolerance=±5% resistance=220 package=THT]
  Part1 = Arduino Uno (Rev3)
  J1 = Piezo Speaker
  R2 = Resistor [tolerance=±5% resistance=1M package=THT]

nets:
  N1: LED1.cathode, R1.Pin_1
  N2: LED1.anode, Part1.D10_PWM/SS
  N3: R1.Pin_0, Part1.GND, J1.pin1, R2.Pin_0
  N4: Part1.A0, J1.pin2, R2.Pin_1

// code stored in the sketch: Untitled2.ino
const int pinne_lampa = 10;
const int pinne_knapp = 2;

#define UPPE LOW
#define NERE HIGH

#define LYS HIGH
#define LYS_INTE LOW

void setup()
{
    pinMode(pinne_knapp, INPUT);
    pinMode(pinne_lampa, OUTPUT);    
}

void loop()
{
    if (digitalRead(pinne_knapp) == NERE)
        digitalWrite(pinne_lampa, LYS);
    else
        digitalWrite(pinne_lampa, LYS_INTE);
}
